// Logisim project 16-bit full adder with sign bit.circ as structural Verilog: 4 circuits, main circuit main
module main (
  input  in_1,
  input  in_2,
  input  in_3,
  input  in_4,
  input  in_5,
  input  in_6,
  input  in_7,
  input  in_8,
  input  in_9,
  input  in_10,
  input  in_11,
  input  in_12,
  input  in_13,
  input  in_14,
  input  in_15,
  input  in_16,
  input  in_17,
  input  in_18,
  input  in_19,
  input  in_20,
  input  in_21,
  input  in_22,
  input  in_23,
  input  in_24,
  input  in_25,
  input  in_26,
  input  in_27,
  input  in_28,
  input  in_29,
  input  in_30,
  input  in_31,
  input  in_32,
  input  in_33,
  output out_34,
  output out_35,
  output out_36,
  output out_37,
  output out_38,
  output out_39,
  output out_40,
  output out_41,
  output out_42,
  output out_43,
  output out_44,
  output out_45,
  output out_46,
  output out_47,
  output out_48,
  output out_49,
  output out_50,
  output out_51
);

  wire n8_bit_adder_with_sign_bit_2_carry_2, n8_bit_adder_with_sign_bit_2_out_19;

  _8_bit_adder_with_sign_bit u_8_bit_adder_with_sign_bit_1 (
    .in_1(in_1), .in_2(in_18), .in_3(in_2), .in_4(in_19), .in_5(in_3), .in_6(in_20), .in_7(in_4),
    .in_8(in_21), .in_9(in_5), .in_10(in_22), .in_11(in_6), .in_12(in_23), .in_13(in_7), .in_14(in_24),
    .in_15(in_8), .in_16(in_25), .in_17(n8_bit_adder_with_sign_bit_2_out_19),
    .Carry(n8_bit_adder_with_sign_bit_2_carry_2), .out_19(out_34), .Carry_2(out_35), .out_21(out_36),
    .out_22(out_37), .out_23(out_38), .out_24(out_39), .out_25(out_40), .out_26(out_41), .out_27(out_42),
    .out_28(out_43));
  _8_bit_adder_with_sign_bit u_8_bit_adder_with_sign_bit_2 (
    .in_1(in_26), .in_2(in_9), .in_3(in_27), .in_4(in_10), .in_5(in_28), .in_6(in_11), .in_7(in_29),
    .in_8(in_12), .in_9(in_30), .in_10(in_13), .in_11(in_31), .in_12(in_14), .in_13(in_32), .in_14(in_15),
    .in_15(in_33), .in_16(in_16), .in_17(in_17), .Carry(in_17), .out_19(n8_bit_adder_with_sign_bit_2_out_19),
    .Carry_2(n8_bit_adder_with_sign_bit_2_carry_2), .out_21(out_44), .out_22(out_45), .out_23(out_46),
    .out_24(out_47), .out_25(out_48), .out_26(out_49), .out_27(out_50), .out_28(out_51));
endmodule

module Half_Adder (
  input  in_1,
  input  in_2,
  output Carry,
  output Sum
);

  and and_1 (Carry, in_1, in_2);
  xor xor_1 (Sum, in_1, in_2);
endmodule

module Full_Adder (
  input  in_1,
  input  in_2,
  input  in_3,
  input  Carry,
  output Carry_2,
  output Sum
);

  wire half_adder_1_carry, half_adder_1_sum, half_adder_2_carry, xor_1_out;

  xor xor_1 (xor_1_out, in_2, in_3);
  Half_Adder half_adder_1 (.in_1(in_1), .in_2(xor_1_out), .Carry(half_adder_1_carry), .Sum(half_adder_1_sum));
  Half_Adder half_adder_2 (.in_1(half_adder_1_sum), .in_2(Carry), .Carry(half_adder_2_carry), .Sum(Sum));
  or or_1 (Carry_2, half_adder_1_carry, half_adder_2_carry);
endmodule

module _8_bit_adder_with_sign_bit (
  input  in_1,
  input  in_2,
  input  in_3,
  input  in_4,
  input  in_5,
  input  in_6,
  input  in_7,
  input  in_8,
  input  in_9,
  input  in_10,
  input  in_11,
  input  in_12,
  input  in_13,
  input  in_14,
  input  in_15,
  input  in_16,
  input  in_17,
  input  Carry,
  output out_19,
  output Carry_2,
  output out_21,
  output out_22,
  output out_23,
  output out_24,
  output out_25,
  output out_26,
  output out_27,
  output out_28
);

  wire full_adder_2_carry_2, full_adder_3_carry_2, full_adder_4_carry_2, full_adder_5_carry_2,
       full_adder_6_carry_2, full_adder_7_carry_2, full_adder_8_carry_2;

  Full_Adder full_adder_1 (
    .in_1(in_1), .in_2(in_2), .in_3(in_17), .Carry(full_adder_2_carry_2), .Carry_2(Carry_2), .Sum(out_21));
  Full_Adder full_adder_2 (
    .in_1(in_3), .in_2(in_4), .in_3(in_17), .Carry(full_adder_3_carry_2), .Carry_2(full_adder_2_carry_2),
    .Sum(out_22));
  Full_Adder full_adder_3 (
    .in_1(in_5), .in_2(in_6), .in_3(in_17), .Carry(full_adder_4_carry_2), .Carry_2(full_adder_3_carry_2),
    .Sum(out_23));
  Full_Adder full_adder_4 (
    .in_1(in_7), .in_2(in_8), .in_3(in_17), .Carry(full_adder_5_carry_2), .Carry_2(full_adder_4_carry_2),
    .Sum(out_24));
  Full_Adder full_adder_5 (
    .in_1(in_9), .in_2(in_10), .in_3(in_17), .Carry(full_adder_6_carry_2), .Carry_2(full_adder_5_carry_2),
    .Sum(out_25));
  Full_Adder full_adder_6 (
    .in_1(in_11), .in_2(in_12), .in_3(in_17), .Carry(full_adder_7_carry_2), .Carry_2(full_adder_6_carry_2),
    .Sum(out_26));
  Full_Adder full_adder_7 (
    .in_1(in_13), .in_2(in_14), .in_3(in_17), .Carry(full_adder_8_carry_2), .Carry_2(full_adder_7_carry_2),
    .Sum(out_27));
  Full_Adder full_adder_8 (
    .in_1(in_15), .in_2(in_16), .in_3(in_17), .Carry(Carry), .Carry_2(full_adder_8_carry_2), .Sum(out_28));

  assign out_19 = in_17;
endmodule
