// Logisim project 4-bit full adder.circ as structural Verilog: 1 circuit, main circuit main
module main (
  input  in_1,
  input  in_2,
  input  in_3,
  input  in_4,
  input  in_5,
  input  in_6,
  input  in_7,
  input  in_8,
  input  carry,
  output carry_2,
  output sum,
  output sum_2,
  output sum_3,
  output sum_4
);

  wire and_1_out, and_2_out, and_3_out, and_4_out, and_5_out, and_6_out, and_7_out, and_8_out, or_2_out,
       or_3_out, or_4_out, xor_1_out, xor_2_out, xor_3_out, xor_4_out;

  and and_1 (and_1_out, in_1, in_2);
  xor xor_1 (xor_1_out, in_1, in_2);
  and and_2 (and_2_out, in_3, in_4);
  xor xor_2 (xor_2_out, in_3, in_4);
  and and_3 (and_3_out, in_5, in_6);
  xor xor_3 (xor_3_out, in_5, in_6);
  and and_4 (and_4_out, in_7, in_8);
  xor xor_4 (xor_4_out, in_7, in_8);
  and and_5 (and_5_out, xor_1_out, or_2_out);
  and and_6 (and_6_out, xor_2_out, or_3_out);
  and and_7 (and_7_out, xor_3_out, or_4_out);
  and and_8 (and_8_out, xor_4_out, carry);
  or or_1 (carry_2, and_1_out, and_5_out);
  xor xor_5 (sum, xor_1_out, or_2_out);
  or or_2 (or_2_out, and_2_out, and_6_out);
  xor xor_6 (sum_2, xor_2_out, or_3_out);
  or or_3 (or_3_out, and_3_out, and_7_out);
  xor xor_7 (sum_3, xor_3_out, or_4_out);
  or or_4 (or_4_out, and_4_out, and_8_out);
  xor xor_8 (sum_4, xor_4_out, carry);
endmodule
