// Logisim project 8-bit full adder.circ as structural Verilog: 3 circuits, main circuit main
module main (
  input  in_1,
  input  in_2,
  input  in_3,
  input  in_4,
  input  in_5,
  input  in_6,
  input  in_7,
  input  in_8,
  input  in_9,
  input  in_10,
  input  in_11,
  input  in_12,
  input  in_13,
  input  in_14,
  input  in_15,
  input  in_16,
  input  carry,
  output carry_2,
  output out_19,
  output out_20,
  output out_21,
  output out_22,
  output out_23,
  output out_24,
  output out_25,
  output out_26
);

  wire full_adder_2_out_4, full_adder_3_out_4, full_adder_4_out_4, full_adder_5_out_4, full_adder_6_out_4,
       full_adder_7_out_4, full_adder_8_out_4;

  Full_Adder full_adder_1 (.in_1(in_1), .in_2(in_2), .in_3(full_adder_2_out_4), .out_4(carry_2), .out_5(out_19));
  Full_Adder full_adder_2 (
    .in_1(in_3), .in_2(in_4), .in_3(full_adder_3_out_4), .out_4(full_adder_2_out_4), .out_5(out_20));
  Full_Adder full_adder_3 (
    .in_1(in_5), .in_2(in_6), .in_3(full_adder_4_out_4), .out_4(full_adder_3_out_4), .out_5(out_21));
  Full_Adder full_adder_4 (
    .in_1(in_7), .in_2(in_8), .in_3(full_adder_5_out_4), .out_4(full_adder_4_out_4), .out_5(out_22));
  Full_Adder full_adder_5 (
    .in_1(in_9), .in_2(in_10), .in_3(full_adder_6_out_4), .out_4(full_adder_5_out_4), .out_5(out_23));
  Full_Adder full_adder_6 (
    .in_1(in_11), .in_2(in_12), .in_3(full_adder_7_out_4), .out_4(full_adder_6_out_4), .out_5(out_24));
  Full_Adder full_adder_7 (
    .in_1(in_13), .in_2(in_14), .in_3(full_adder_8_out_4), .out_4(full_adder_7_out_4), .out_5(out_25));
  Full_Adder full_adder_8 (.in_1(in_15), .in_2(in_16), .in_3(carry), .out_4(full_adder_8_out_4), .out_5(out_26));
endmodule

module Half_Adder (
  input  in_1,
  input  in_2,
  output out_3,
  output out_4
);

  and and_1 (out_3, in_1, in_2);
  xor xor_1 (out_4, in_1, in_2);
endmodule

module Full_Adder (
  input  in_1,
  input  in_2,
  input  in_3,
  output out_4,
  output out_5
);

  wire half_adder_1_out_3, half_adder_1_out_4, half_adder_2_out_3;

  Half_Adder half_adder_1 (.in_1(in_1), .in_2(in_2), .out_3(half_adder_1_out_3), .out_4(half_adder_1_out_4));
  Half_Adder half_adder_2 (.in_1(half_adder_1_out_4), .in_2(in_3), .out_3(half_adder_2_out_3), .out_4(out_5));
  or or_1 (out_4, half_adder_1_out_3, half_adder_2_out_3);
endmodule
