// Logisim project 8-bit multiplication.circ as structural Verilog: 2 circuits, main circuit main
module main (
  input  in_1,
  input  in_2,
  input  in_3,
  input  in_4,
  input  in_5,
  input  in_6,
  input  in_7,
  input  in_8,
  output out_9,
  output out_10,
  output out_11,
  output out_12,
  output out_13,
  output out_14,
  output out_15,
  output out_16,
  output out_17
);

  wire main_1_out_19, main_1_out_20, main_1_out_21, main_1_out_22, main_1_out_23, main_1_out_24,
       main_1_out_25, main_1_out_26, main_2_out_12, main_2_out_13, main_2_out_14, main_2_out_15,
       main_2_out_16, main_2_out_17, main_2_out_18, main_2_out_19, main_4_out_12, main_4_out_13,
       main_4_out_14, main_4_out_15, main_4_out_16, main_4_out_17, main_4_out_18, main_4_out_19,
       main_5_out_19, main_5_out_20, main_5_out_21, main_5_out_22, main_5_out_23, main_5_out_24,
       main_5_out_25, main_5_out_26, main_6_out_12, main_6_out_13, main_6_out_14, main_6_out_15,
       main_6_out_16, main_6_out_17, main_6_out_18, main_6_out_19, main_7_out_12, main_7_out_13,
       main_7_out_14, main_7_out_15, main_7_out_16, main_7_out_17, main_7_out_18, main_7_out_19,
       n8_bit_s_r_1_out_10, n8_bit_s_r_1_out_11, n8_bit_s_r_1_out_12, n8_bit_s_r_1_out_13,
       n8_bit_s_r_1_out_14, n8_bit_s_r_1_out_15, n8_bit_s_r_1_out_16, n8_bit_s_r_1_out_17,
       n8_bit_s_r_2_out_10, n8_bit_s_r_2_out_11, n8_bit_s_r_2_out_12, n8_bit_s_r_2_out_13,
       n8_bit_s_r_2_out_14, n8_bit_s_r_2_out_15, n8_bit_s_r_2_out_16, n8_bit_s_r_2_out_17,
       n8_bit_s_r_3_out_10, n8_bit_s_r_3_out_11, n8_bit_s_r_3_out_12, n8_bit_s_r_3_out_13,
       n8_bit_s_r_3_out_14, n8_bit_s_r_3_out_15, n8_bit_s_r_3_out_16, n8_bit_s_r_3_out_17,
       n8_bit_s_r_4_out_10, n8_bit_s_r_4_out_11, n8_bit_s_r_4_out_12, n8_bit_s_r_4_out_13,
       n8_bit_s_r_4_out_14, n8_bit_s_r_4_out_15, n8_bit_s_r_4_out_16, n8_bit_s_r_4_out_17;

  _8_bit_full_adder_main main_1 (
    .in_1(n8_bit_s_r_1_out_10), .in_2(n8_bit_s_r_2_out_10), .in_3(n8_bit_s_r_1_out_11),
    .in_4(n8_bit_s_r_2_out_11), .in_5(n8_bit_s_r_1_out_12), .in_6(n8_bit_s_r_2_out_12),
    .in_7(n8_bit_s_r_1_out_13), .in_8(n8_bit_s_r_2_out_13), .in_9(n8_bit_s_r_1_out_14),
    .in_10(n8_bit_s_r_2_out_14), .in_11(n8_bit_s_r_1_out_15), .in_12(n8_bit_s_r_2_out_15),
    .in_13(n8_bit_s_r_1_out_16), .in_14(n8_bit_s_r_2_out_16), .in_15(n8_bit_s_r_1_out_17),
    .in_16(n8_bit_s_r_2_out_17), .carry(1'b0), .out_19(main_1_out_19), .out_20(main_1_out_20),
    .out_21(main_1_out_21), .out_22(main_1_out_22), .out_23(main_1_out_23), .out_24(main_1_out_24),
    .out_25(main_1_out_25), .out_26(main_1_out_26));  // open: carry_2
  _8_bit_S_R u_8_bit_s_r_1 (
    .in_2(main_2_out_12), .in_3(main_2_out_13), .in_4(main_2_out_14), .in_5(main_2_out_15),
    .in_6(main_2_out_16), .in_7(main_2_out_17), .in_8(main_2_out_18), .in_9(main_2_out_19),
    .S_R__S___1__R___0(in_8), .out_10(n8_bit_s_r_1_out_10), .out_11(n8_bit_s_r_1_out_11),
    .out_12(n8_bit_s_r_1_out_12), .out_13(n8_bit_s_r_1_out_13), .out_14(n8_bit_s_r_1_out_14),
    .out_15(n8_bit_s_r_1_out_15), .out_16(n8_bit_s_r_1_out_16), .out_17(n8_bit_s_r_1_out_17));
  _8_bit_left_shifter_main main_2 (
    .shift(1'b0), .carry(1'b0), .out_12(main_2_out_12), .out_13(main_2_out_13), .out_14(main_2_out_14),
    .out_15(main_2_out_15), .out_16(main_2_out_16), .out_17(main_2_out_17), .out_18(main_2_out_18),
    .out_19(main_2_out_19), .in_3(1'b0), .in_4(1'b0), .in_5(1'b0), .in_6(1'b0), .in_7(in_1), .in_8(in_2),
    .in_9(in_3), .in_10(in_4));  // open: carry_2
  _8_bit_full_adder_main main_3 (
    .in_1(main_1_out_19), .in_2(main_5_out_19), .in_3(main_1_out_20), .in_4(main_5_out_20),
    .in_5(main_1_out_21), .in_6(main_5_out_21), .in_7(main_1_out_22), .in_8(main_5_out_22),
    .in_9(main_1_out_23), .in_10(main_5_out_23), .in_11(main_1_out_24), .in_12(main_5_out_24),
    .in_13(main_1_out_25), .in_14(main_5_out_25), .in_15(main_1_out_26), .in_16(main_5_out_26), .carry(1'b0),
    .out_19(out_10), .out_20(out_11), .out_21(out_12), .out_22(out_13), .out_23(out_14), .out_24(out_15),
    .out_25(out_16), .out_26(out_17), .carry_2(out_9));
  _8_bit_S_R u_8_bit_s_r_2 (
    .in_2(main_4_out_12), .in_3(main_4_out_13), .in_4(main_4_out_14), .in_5(main_4_out_15),
    .in_6(main_4_out_16), .in_7(main_4_out_17), .in_8(main_4_out_18), .in_9(main_4_out_19),
    .S_R__S___1__R___0(in_7), .out_10(n8_bit_s_r_2_out_10), .out_11(n8_bit_s_r_2_out_11),
    .out_12(n8_bit_s_r_2_out_12), .out_13(n8_bit_s_r_2_out_13), .out_14(n8_bit_s_r_2_out_14),
    .out_15(n8_bit_s_r_2_out_15), .out_16(n8_bit_s_r_2_out_16), .out_17(n8_bit_s_r_2_out_17));
  _8_bit_left_shifter_main main_4 (
    .shift(1'b1), .carry(1'b0), .out_12(main_4_out_12), .out_13(main_4_out_13), .out_14(main_4_out_14),
    .out_15(main_4_out_15), .out_16(main_4_out_16), .out_17(main_4_out_17), .out_18(main_4_out_18),
    .out_19(main_4_out_19), .in_3(main_2_out_12), .in_4(main_2_out_13), .in_5(main_2_out_14),
    .in_6(main_2_out_15), .in_7(main_2_out_16), .in_8(main_2_out_17), .in_9(main_2_out_18),
    .in_10(main_2_out_19));  // open: carry_2
  _8_bit_full_adder_main main_5 (
    .in_1(n8_bit_s_r_3_out_10), .in_2(n8_bit_s_r_4_out_10), .in_3(n8_bit_s_r_3_out_11),
    .in_4(n8_bit_s_r_4_out_11), .in_5(n8_bit_s_r_3_out_12), .in_6(n8_bit_s_r_4_out_12),
    .in_7(n8_bit_s_r_3_out_13), .in_8(n8_bit_s_r_4_out_13), .in_9(n8_bit_s_r_3_out_14),
    .in_10(n8_bit_s_r_4_out_14), .in_11(n8_bit_s_r_3_out_15), .in_12(n8_bit_s_r_4_out_15),
    .in_13(n8_bit_s_r_3_out_16), .in_14(n8_bit_s_r_4_out_16), .in_15(n8_bit_s_r_3_out_17),
    .in_16(n8_bit_s_r_4_out_17), .carry(1'b0), .out_19(main_5_out_19), .out_20(main_5_out_20),
    .out_21(main_5_out_21), .out_22(main_5_out_22), .out_23(main_5_out_23), .out_24(main_5_out_24),
    .out_25(main_5_out_25), .out_26(main_5_out_26));  // open: carry_2
  _8_bit_S_R u_8_bit_s_r_3 (
    .in_2(main_6_out_12), .in_3(main_6_out_13), .in_4(main_6_out_14), .in_5(main_6_out_15),
    .in_6(main_6_out_16), .in_7(main_6_out_17), .in_8(main_6_out_18), .in_9(main_6_out_19),
    .S_R__S___1__R___0(in_6), .out_10(n8_bit_s_r_3_out_10), .out_11(n8_bit_s_r_3_out_11),
    .out_12(n8_bit_s_r_3_out_12), .out_13(n8_bit_s_r_3_out_13), .out_14(n8_bit_s_r_3_out_14),
    .out_15(n8_bit_s_r_3_out_15), .out_16(n8_bit_s_r_3_out_16), .out_17(n8_bit_s_r_3_out_17));
  _8_bit_left_shifter_main main_6 (
    .shift(1'b1), .carry(1'b0), .out_12(main_6_out_12), .out_13(main_6_out_13), .out_14(main_6_out_14),
    .out_15(main_6_out_15), .out_16(main_6_out_16), .out_17(main_6_out_17), .out_18(main_6_out_18),
    .out_19(main_6_out_19), .in_3(main_4_out_12), .in_4(main_4_out_13), .in_5(main_4_out_14),
    .in_6(main_4_out_15), .in_7(main_4_out_16), .in_8(main_4_out_17), .in_9(main_4_out_18),
    .in_10(main_4_out_19));  // open: carry_2
  _8_bit_S_R u_8_bit_s_r_4 (
    .in_2(main_7_out_12), .in_3(main_7_out_13), .in_4(main_7_out_14), .in_5(main_7_out_15),
    .in_6(main_7_out_16), .in_7(main_7_out_17), .in_8(main_7_out_18), .in_9(main_7_out_19),
    .S_R__S___1__R___0(in_5), .out_10(n8_bit_s_r_4_out_10), .out_11(n8_bit_s_r_4_out_11),
    .out_12(n8_bit_s_r_4_out_12), .out_13(n8_bit_s_r_4_out_13), .out_14(n8_bit_s_r_4_out_14),
    .out_15(n8_bit_s_r_4_out_15), .out_16(n8_bit_s_r_4_out_16), .out_17(n8_bit_s_r_4_out_17));
  _8_bit_left_shifter_main main_7 (
    .shift(1'b1), .carry(1'b0), .out_12(main_7_out_12), .out_13(main_7_out_13), .out_14(main_7_out_14),
    .out_15(main_7_out_15), .out_16(main_7_out_16), .out_17(main_7_out_17), .out_18(main_7_out_18),
    .out_19(main_7_out_19), .in_3(main_6_out_12), .in_4(main_6_out_13), .in_5(main_6_out_14),
    .in_6(main_6_out_15), .in_7(main_6_out_16), .in_8(main_6_out_17), .in_9(main_6_out_18),
    .in_10(main_6_out_19));  // open: carry_2
endmodule

module _8_bit_S_R (
  input  S_R__S___1__R___0,
  input  in_2,
  input  in_3,
  input  in_4,
  input  in_5,
  input  in_6,
  input  in_7,
  input  in_8,
  input  in_9,
  output out_10,
  output out_11,
  output out_12,
  output out_13,
  output out_14,
  output out_15,
  output out_16,
  output out_17
);

  and and_1 (out_11, in_3, S_R__S___1__R___0);
  and and_2 (out_10, in_2, S_R__S___1__R___0);
  and and_3 (out_12, in_4, S_R__S___1__R___0);
  and and_4 (out_13, in_5, S_R__S___1__R___0);
  and and_5 (out_15, in_7, S_R__S___1__R___0);
  and and_6 (out_14, in_6, S_R__S___1__R___0);
  and and_7 (out_16, in_8, S_R__S___1__R___0);
  and and_8 (out_17, in_9, S_R__S___1__R___0);
endmodule
