// Logisim project 8-bit decimal to 3 seven segment signals.circ as structural Verilog: 5 circuits, main circuit main
module main (
  input  period_2,
  input  period_1,
  input  period_0,
  input  in_4,
  input  in_5,
  input  in_6,
  input  in_7,
  input  in_8,
  input  in_9,
  input  in_10,
  input  in_11,
  output T0,
  output T1,
  output T2,
  output T3,
  output B0,
  output B1,
  output B2,
  output period,
  output T0_2,
  output T1_2,
  output T2_2,
  output T3_2,
  output B0_2,
  output B1_2,
  output B2_2,
  output period_3,
  output T0_3,
  output T1_3,
  output T2_3,
  output T3_3,
  output B0_3,
  output B1_3,
  output B2_3,
  output period_4
);

  wire conditional_adder_1_out_5, conditional_adder_1_out_6, conditional_adder_1_out_7,
       conditional_adder_1_out_8, conditional_adder_2_out_5, conditional_adder_2_out_6,
       conditional_adder_2_out_7, conditional_adder_2_out_8, conditional_adder_3_out_5,
       conditional_adder_3_out_6, conditional_adder_3_out_7, conditional_adder_3_out_8,
       conditional_adder_4_out_5, conditional_adder_4_out_6, conditional_adder_4_out_7,
       conditional_adder_4_out_8, conditional_adder_5_out_5, conditional_adder_5_out_6,
       conditional_adder_5_out_7, conditional_adder_5_out_8, conditional_adder_6_out_5,
       conditional_adder_6_out_6, conditional_adder_6_out_7, conditional_adder_6_out_8,
       conditional_adder_7_out_5, conditional_adder_7_out_6, conditional_adder_7_out_7,
       conditional_adder_7_out_8, conditional_adder_8_out_5, conditional_adder_8_out_6,
       conditional_adder_8_out_7, conditional_adder_8_out_8, conditional_adder_9_out_5,
       conditional_adder_9_out_6, conditional_adder_9_out_7, conditional_adder_9_out_8,
       conditional_adder_10_out_5, conditional_adder_10_out_6, conditional_adder_10_out_7,
       conditional_adder_10_out_8, conditional_adder_11_out_5, conditional_adder_11_out_6,
       conditional_adder_11_out_7, conditional_adder_11_out_8, conditional_adder_12_out_5,
       conditional_adder_12_out_6, conditional_adder_12_out_7, conditional_adder_12_out_8,
       conditional_adder_13_out_5, conditional_adder_13_out_6, conditional_adder_13_out_7,
       conditional_adder_13_out_8, conditional_adder_14_out_5, conditional_adder_14_out_6,
       conditional_adder_14_out_7, conditional_adder_14_out_8, conditional_adder_15_out_5,
       conditional_adder_15_out_6, conditional_adder_15_out_7, conditional_adder_15_out_8,
       conditional_adder_16_out_5, conditional_adder_16_out_6, conditional_adder_16_out_7,
       conditional_adder_16_out_8, conditional_adder_17_out_5, conditional_adder_17_out_6,
       conditional_adder_17_out_7, conditional_adder_17_out_8, conditional_adder_18_out_5,
       conditional_adder_18_out_6, conditional_adder_18_out_7, conditional_adder_18_out_8,
       conditional_adder_19_out_5, conditional_adder_19_out_6, conditional_adder_19_out_7,
       conditional_adder_19_out_8, conditional_adder_20_out_5, conditional_adder_20_out_6,
       conditional_adder_20_out_7, conditional_adder_20_out_8, conditional_adder_21_out_5,
       conditional_adder_21_out_6, conditional_adder_21_out_7, conditional_adder_21_out_8, main_1_carry_2,
       main_2_carry_2, main_2_out_12, main_2_out_13, main_2_out_14, main_2_out_15, main_2_out_16,
       main_2_out_17, main_2_out_18, main_2_out_19, main_3_carry_2, main_3_out_12, main_3_out_13,
       main_3_out_14, main_3_out_15, main_3_out_16, main_3_out_17, main_3_out_18, main_3_out_19,
       main_4_carry_2, main_4_out_12, main_4_out_13, main_4_out_14, main_4_out_15, main_4_out_16,
       main_4_out_17, main_4_out_18, main_4_out_19, main_5_carry_2, main_5_out_12, main_5_out_13,
       main_5_out_14, main_5_out_15, main_5_out_16, main_5_out_17, main_5_out_18, main_5_out_19,
       main_6_carry_2, main_6_out_12, main_6_out_13, main_6_out_14, main_6_out_15, main_6_out_16,
       main_6_out_17, main_6_out_18, main_6_out_19, main_7_carry_2, main_7_out_12, main_7_out_13,
       main_7_out_14, main_7_out_15, main_7_out_16, main_7_out_17, main_7_out_18, main_7_out_19,
       main_8_carry_2, main_8_out_12, main_8_out_13, main_8_out_14, main_8_out_15, main_8_out_16,
       main_8_out_17, main_8_out_18, main_8_out_19, n4_bit_shifter_1_out_8, n4_bit_shifter_1_out_9,
       n4_bit_shifter_1_out_10, n4_bit_shifter_1_out_11, n4_bit_shifter_2_out_8, n4_bit_shifter_2_out_9,
       n4_bit_shifter_2_out_10, n4_bit_shifter_2_out_11, n4_bit_shifter_3_out_8, n4_bit_shifter_3_out_9,
       n4_bit_shifter_3_out_10, n4_bit_shifter_3_out_11, n4_bit_shifter_4_out_8, n4_bit_shifter_4_out_9,
       n4_bit_shifter_4_out_10, n4_bit_shifter_4_out_11, n4_bit_shifter_5_out_8, n4_bit_shifter_5_out_9,
       n4_bit_shifter_5_out_10, n4_bit_shifter_5_out_11, n4_bit_shifter_6_out_8, n4_bit_shifter_6_out_9,
       n4_bit_shifter_6_out_10, n4_bit_shifter_6_out_11, n4_bit_shifter_7_out_8, n4_bit_shifter_7_out_9,
       n4_bit_shifter_7_out_10, n4_bit_shifter_7_out_11, n4_bit_shifter_8_out_8, n4_bit_shifter_8_out_9,
       n4_bit_shifter_8_out_10, n4_bit_shifter_8_out_11, n4_bit_shifter_9_carry_2, n4_bit_shifter_9_out_8,
       n4_bit_shifter_9_out_9, n4_bit_shifter_9_out_10, n4_bit_shifter_9_out_11, n4_bit_shifter_10_carry_2,
       n4_bit_shifter_10_out_8, n4_bit_shifter_10_out_9, n4_bit_shifter_10_out_10, n4_bit_shifter_10_out_11,
       n4_bit_shifter_11_carry_2, n4_bit_shifter_11_out_8, n4_bit_shifter_11_out_9, n4_bit_shifter_11_out_10,
       n4_bit_shifter_11_out_11, n4_bit_shifter_12_carry_2, n4_bit_shifter_12_out_8, n4_bit_shifter_12_out_9,
       n4_bit_shifter_12_out_10, n4_bit_shifter_12_out_11, n4_bit_shifter_13_carry_2,
       n4_bit_shifter_13_out_8, n4_bit_shifter_13_out_9, n4_bit_shifter_13_out_10, n4_bit_shifter_13_out_11,
       n4_bit_shifter_14_carry_2, n4_bit_shifter_14_out_8, n4_bit_shifter_14_out_9, n4_bit_shifter_14_out_10,
       n4_bit_shifter_14_out_11, n4_bit_shifter_15_carry_2, n4_bit_shifter_15_out_8, n4_bit_shifter_15_out_9,
       n4_bit_shifter_15_out_10, n4_bit_shifter_15_out_11, n4_bit_shifter_16_carry_2,
       n4_bit_shifter_16_out_8, n4_bit_shifter_16_out_9, n4_bit_shifter_16_out_10, n4_bit_shifter_16_out_11,
       n4_bit_shifter_17_carry_2, n4_bit_shifter_17_out_8, n4_bit_shifter_17_out_9, n4_bit_shifter_17_out_10,
       n4_bit_shifter_17_out_11, n4_bit_shifter_18_carry_2, n4_bit_shifter_18_out_8, n4_bit_shifter_18_out_9,
       n4_bit_shifter_18_out_10, n4_bit_shifter_18_out_11, n4_bit_shifter_19_carry_2,
       n4_bit_shifter_19_out_8, n4_bit_shifter_19_out_9, n4_bit_shifter_19_out_10, n4_bit_shifter_19_out_11,
       n4_bit_shifter_20_carry_2, n4_bit_shifter_20_out_9, n4_bit_shifter_20_out_10,
       n4_bit_shifter_20_out_11, n4_bit_shifter_21_carry_2, n4_bit_shifter_21_out_8, n4_bit_shifter_21_out_9,
       n4_bit_shifter_21_out_10, n4_bit_shifter_21_out_11, n4_bit_shifter_22_carry_2,
       n4_bit_shifter_22_out_8, n4_bit_shifter_22_out_9, n4_bit_shifter_22_out_10, n4_bit_shifter_22_out_11,
       n4_bit_shifter_23_carry_2, n4_bit_shifter_23_out_8, n4_bit_shifter_23_out_9, n4_bit_shifter_23_out_10,
       n4_bit_shifter_23_out_11, n4_bit_shifter_24_carry_2, n4_bit_shifter_24_out_8, n4_bit_shifter_24_out_9,
       n4_bit_shifter_24_out_10, n4_bit_shifter_24_out_11, not_1_out;

  not not_1 (not_1_out, 1'b1);
  binary_to_0_9_7_segment_signals binary_to_0_9_7_segment_signals_1 (
    .T0(T0), .T1(T1), .T2(T2), .T3(T3), .B0(B0), .B1(B1), .B2(B2), .period_2(period),
    .in_1(n4_bit_shifter_4_out_8), .in_2(n4_bit_shifter_4_out_9), .in_3(n4_bit_shifter_4_out_10),
    .in_4(n4_bit_shifter_4_out_11), .period(period_0));
  conditional_adder conditional_adder_1 (
    .out_5(conditional_adder_1_out_5), .out_6(conditional_adder_1_out_6), .out_7(conditional_adder_1_out_7),
    .out_8(conditional_adder_1_out_8), .in_1(n4_bit_shifter_7_out_8), .in_2(n4_bit_shifter_7_out_9),
    .in_3(n4_bit_shifter_7_out_10), .in_4(n4_bit_shifter_7_out_11));
  conditional_adder conditional_adder_2 (
    .out_5(conditional_adder_2_out_5), .out_6(conditional_adder_2_out_6), .out_7(conditional_adder_2_out_7),
    .out_8(conditional_adder_2_out_8), .in_1(n4_bit_shifter_8_out_8), .in_2(n4_bit_shifter_8_out_9),
    .in_3(n4_bit_shifter_8_out_10), .in_4(n4_bit_shifter_8_out_11));
  conditional_adder conditional_adder_3 (
    .out_5(conditional_adder_3_out_5), .out_6(conditional_adder_3_out_6), .out_7(conditional_adder_3_out_7),
    .out_8(conditional_adder_3_out_8), .in_1(n4_bit_shifter_1_out_8), .in_2(n4_bit_shifter_1_out_9),
    .in_3(n4_bit_shifter_1_out_10), .in_4(n4_bit_shifter_1_out_11));
  _4_bit_shifter u_4_bit_shifter_1 (
    .shift(1'b1), .carry(n4_bit_shifter_13_carry_2), .out_8(n4_bit_shifter_1_out_8),
    .out_9(n4_bit_shifter_1_out_9), .out_10(n4_bit_shifter_1_out_10), .out_11(n4_bit_shifter_1_out_11),
    .in_3(conditional_adder_4_out_5), .in_4(conditional_adder_4_out_6), .in_5(conditional_adder_4_out_7),
    .in_6(conditional_adder_4_out_8));  // open: carry_2
  conditional_adder conditional_adder_4 (
    .out_5(conditional_adder_4_out_5), .out_6(conditional_adder_4_out_6), .out_7(conditional_adder_4_out_7),
    .out_8(conditional_adder_4_out_8), .in_1(n4_bit_shifter_2_out_8), .in_2(n4_bit_shifter_2_out_9),
    .in_3(n4_bit_shifter_2_out_10), .in_4(n4_bit_shifter_2_out_11));
  _4_bit_shifter u_4_bit_shifter_2 (
    .shift(1'b1), .carry(n4_bit_shifter_14_carry_2), .out_8(n4_bit_shifter_2_out_8),
    .out_9(n4_bit_shifter_2_out_9), .out_10(n4_bit_shifter_2_out_10), .out_11(n4_bit_shifter_2_out_11),
    .in_3(conditional_adder_5_out_5), .in_4(conditional_adder_5_out_6), .in_5(conditional_adder_5_out_7),
    .in_6(conditional_adder_5_out_8));  // open: carry_2
  conditional_adder conditional_adder_5 (
    .out_5(conditional_adder_5_out_5), .out_6(conditional_adder_5_out_6), .out_7(conditional_adder_5_out_7),
    .out_8(conditional_adder_5_out_8), .in_1(n4_bit_shifter_3_out_8), .in_2(n4_bit_shifter_3_out_9),
    .in_3(n4_bit_shifter_3_out_10), .in_4(n4_bit_shifter_3_out_11));
  _4_bit_shifter u_4_bit_shifter_3 (
    .shift(1'b1), .carry(n4_bit_shifter_15_carry_2), .out_8(n4_bit_shifter_3_out_8),
    .out_9(n4_bit_shifter_3_out_9), .out_10(n4_bit_shifter_3_out_10), .out_11(n4_bit_shifter_3_out_11),
    .in_3(not_1_out), .in_4(not_1_out), .in_5(not_1_out), .in_6(not_1_out));  // open: carry_2
  _4_bit_shifter u_4_bit_shifter_4 (
    .shift(1'b1), .carry(n4_bit_shifter_16_carry_2), .out_8(n4_bit_shifter_4_out_8),
    .out_9(n4_bit_shifter_4_out_9), .out_10(n4_bit_shifter_4_out_10), .out_11(n4_bit_shifter_4_out_11),
    .in_3(conditional_adder_6_out_5), .in_4(conditional_adder_6_out_6), .in_5(conditional_adder_6_out_7),
    .in_6(conditional_adder_6_out_8));  // open: carry_2
  conditional_adder conditional_adder_6 (
    .out_5(conditional_adder_6_out_5), .out_6(conditional_adder_6_out_6), .out_7(conditional_adder_6_out_7),
    .out_8(conditional_adder_6_out_8), .in_1(n4_bit_shifter_5_out_8), .in_2(n4_bit_shifter_5_out_9),
    .in_3(n4_bit_shifter_5_out_10), .in_4(n4_bit_shifter_5_out_11));
  _4_bit_shifter u_4_bit_shifter_5 (
    .shift(1'b1), .carry(n4_bit_shifter_9_carry_2), .out_8(n4_bit_shifter_5_out_8),
    .out_9(n4_bit_shifter_5_out_9), .out_10(n4_bit_shifter_5_out_10), .out_11(n4_bit_shifter_5_out_11),
    .in_3(conditional_adder_7_out_5), .in_4(conditional_adder_7_out_6), .in_5(conditional_adder_7_out_7),
    .in_6(conditional_adder_7_out_8));  // open: carry_2
  conditional_adder conditional_adder_7 (
    .out_5(conditional_adder_7_out_5), .out_6(conditional_adder_7_out_6), .out_7(conditional_adder_7_out_7),
    .out_8(conditional_adder_7_out_8), .in_1(n4_bit_shifter_6_out_8), .in_2(n4_bit_shifter_6_out_9),
    .in_3(n4_bit_shifter_6_out_10), .in_4(n4_bit_shifter_6_out_11));
  _4_bit_shifter u_4_bit_shifter_6 (
    .shift(1'b1), .carry(n4_bit_shifter_10_carry_2), .out_8(n4_bit_shifter_6_out_8),
    .out_9(n4_bit_shifter_6_out_9), .out_10(n4_bit_shifter_6_out_10), .out_11(n4_bit_shifter_6_out_11),
    .in_3(conditional_adder_1_out_5), .in_4(conditional_adder_1_out_6), .in_5(conditional_adder_1_out_7),
    .in_6(conditional_adder_1_out_8));  // open: carry_2
  _4_bit_shifter u_4_bit_shifter_7 (
    .shift(1'b1), .carry(n4_bit_shifter_11_carry_2), .out_8(n4_bit_shifter_7_out_8),
    .out_9(n4_bit_shifter_7_out_9), .out_10(n4_bit_shifter_7_out_10), .out_11(n4_bit_shifter_7_out_11),
    .in_3(conditional_adder_2_out_5), .in_4(conditional_adder_2_out_6), .in_5(conditional_adder_2_out_7),
    .in_6(conditional_adder_2_out_8));  // open: carry_2
  _4_bit_shifter u_4_bit_shifter_8 (
    .shift(1'b1), .carry(n4_bit_shifter_12_carry_2), .out_8(n4_bit_shifter_8_out_8),
    .out_9(n4_bit_shifter_8_out_9), .out_10(n4_bit_shifter_8_out_10), .out_11(n4_bit_shifter_8_out_11),
    .in_3(conditional_adder_3_out_5), .in_4(conditional_adder_3_out_6), .in_5(conditional_adder_3_out_7),
    .in_6(conditional_adder_3_out_8));  // open: carry_2
  conditional_adder conditional_adder_8 (
    .out_5(conditional_adder_8_out_5), .out_6(conditional_adder_8_out_6), .out_7(conditional_adder_8_out_7),
    .out_8(conditional_adder_8_out_8), .in_1(n4_bit_shifter_15_out_8), .in_2(n4_bit_shifter_15_out_9),
    .in_3(n4_bit_shifter_15_out_10), .in_4(n4_bit_shifter_15_out_11));
  binary_to_0_9_7_segment_signals binary_to_0_9_7_segment_signals_2 (
    .T0(T0_2), .T1(T1_2), .T2(T2_2), .T3(T3_2), .B0(B0_2), .B1(B1_2), .B2(B2_2), .period_2(period_3),
    .in_1(n4_bit_shifter_16_out_8), .in_2(n4_bit_shifter_16_out_9), .in_3(n4_bit_shifter_16_out_10),
    .in_4(n4_bit_shifter_16_out_11), .period(period_1));
  conditional_adder conditional_adder_9 (
    .out_5(conditional_adder_9_out_5), .out_6(conditional_adder_9_out_6), .out_7(conditional_adder_9_out_7),
    .out_8(conditional_adder_9_out_8), .in_1(n4_bit_shifter_9_out_8), .in_2(n4_bit_shifter_9_out_9),
    .in_3(n4_bit_shifter_9_out_10), .in_4(n4_bit_shifter_9_out_11));
  _4_bit_shifter u_4_bit_shifter_9 (
    .shift(1'b1), .carry(n4_bit_shifter_21_carry_2), .carry_2(n4_bit_shifter_9_carry_2),
    .out_8(n4_bit_shifter_9_out_8), .out_9(n4_bit_shifter_9_out_9), .out_10(n4_bit_shifter_9_out_10),
    .out_11(n4_bit_shifter_9_out_11), .in_3(conditional_adder_10_out_5), .in_4(conditional_adder_10_out_6),
    .in_5(conditional_adder_10_out_7), .in_6(conditional_adder_10_out_8));
  conditional_adder conditional_adder_10 (
    .out_5(conditional_adder_10_out_5), .out_6(conditional_adder_10_out_6),
    .out_7(conditional_adder_10_out_7), .out_8(conditional_adder_10_out_8), .in_1(n4_bit_shifter_10_out_8),
    .in_2(n4_bit_shifter_10_out_9), .in_3(n4_bit_shifter_10_out_10), .in_4(n4_bit_shifter_10_out_11));
  _4_bit_shifter u_4_bit_shifter_10 (
    .shift(1'b1), .carry(n4_bit_shifter_22_carry_2), .carry_2(n4_bit_shifter_10_carry_2),
    .out_8(n4_bit_shifter_10_out_8), .out_9(n4_bit_shifter_10_out_9), .out_10(n4_bit_shifter_10_out_10),
    .out_11(n4_bit_shifter_10_out_11), .in_3(conditional_adder_11_out_5), .in_4(conditional_adder_11_out_6),
    .in_5(conditional_adder_11_out_7), .in_6(conditional_adder_11_out_8));
  conditional_adder conditional_adder_11 (
    .out_5(conditional_adder_11_out_5), .out_6(conditional_adder_11_out_6),
    .out_7(conditional_adder_11_out_7), .out_8(conditional_adder_11_out_8), .in_1(n4_bit_shifter_11_out_8),
    .in_2(n4_bit_shifter_11_out_9), .in_3(n4_bit_shifter_11_out_10), .in_4(n4_bit_shifter_11_out_11));
  _4_bit_shifter u_4_bit_shifter_11 (
    .shift(1'b1), .carry(n4_bit_shifter_23_carry_2), .carry_2(n4_bit_shifter_11_carry_2),
    .out_8(n4_bit_shifter_11_out_8), .out_9(n4_bit_shifter_11_out_9), .out_10(n4_bit_shifter_11_out_10),
    .out_11(n4_bit_shifter_11_out_11), .in_3(conditional_adder_12_out_5), .in_4(conditional_adder_12_out_6),
    .in_5(conditional_adder_12_out_7), .in_6(conditional_adder_12_out_8));
  conditional_adder conditional_adder_12 (
    .out_5(conditional_adder_12_out_5), .out_6(conditional_adder_12_out_6),
    .out_7(conditional_adder_12_out_7), .out_8(conditional_adder_12_out_8), .in_1(n4_bit_shifter_12_out_8),
    .in_2(n4_bit_shifter_12_out_9), .in_3(n4_bit_shifter_12_out_10), .in_4(n4_bit_shifter_12_out_11));
  _4_bit_shifter u_4_bit_shifter_12 (
    .shift(1'b1), .carry(n4_bit_shifter_24_carry_2), .carry_2(n4_bit_shifter_12_carry_2),
    .out_8(n4_bit_shifter_12_out_8), .out_9(n4_bit_shifter_12_out_9), .out_10(n4_bit_shifter_12_out_10),
    .out_11(n4_bit_shifter_12_out_11), .in_3(conditional_adder_13_out_5), .in_4(conditional_adder_13_out_6),
    .in_5(conditional_adder_13_out_7), .in_6(conditional_adder_13_out_8));
  conditional_adder conditional_adder_13 (
    .out_5(conditional_adder_13_out_5), .out_6(conditional_adder_13_out_6),
    .out_7(conditional_adder_13_out_7), .out_8(conditional_adder_13_out_8), .in_1(n4_bit_shifter_13_out_8),
    .in_2(n4_bit_shifter_13_out_9), .in_3(n4_bit_shifter_13_out_10), .in_4(n4_bit_shifter_13_out_11));
  _4_bit_shifter u_4_bit_shifter_13 (
    .shift(1'b1), .carry(n4_bit_shifter_17_carry_2), .carry_2(n4_bit_shifter_13_carry_2),
    .out_8(n4_bit_shifter_13_out_8), .out_9(n4_bit_shifter_13_out_9), .out_10(n4_bit_shifter_13_out_10),
    .out_11(n4_bit_shifter_13_out_11), .in_3(conditional_adder_14_out_5), .in_4(conditional_adder_14_out_6),
    .in_5(conditional_adder_14_out_7), .in_6(conditional_adder_14_out_8));
  conditional_adder conditional_adder_14 (
    .out_5(conditional_adder_14_out_5), .out_6(conditional_adder_14_out_6),
    .out_7(conditional_adder_14_out_7), .out_8(conditional_adder_14_out_8), .in_1(n4_bit_shifter_14_out_8),
    .in_2(n4_bit_shifter_14_out_9), .in_3(n4_bit_shifter_14_out_10), .in_4(n4_bit_shifter_14_out_11));
  _4_bit_shifter u_4_bit_shifter_14 (
    .shift(1'b1), .carry(n4_bit_shifter_18_carry_2), .carry_2(n4_bit_shifter_14_carry_2),
    .out_8(n4_bit_shifter_14_out_8), .out_9(n4_bit_shifter_14_out_9), .out_10(n4_bit_shifter_14_out_10),
    .out_11(n4_bit_shifter_14_out_11), .in_3(conditional_adder_8_out_5), .in_4(conditional_adder_8_out_6),
    .in_5(conditional_adder_8_out_7), .in_6(conditional_adder_8_out_8));
  _4_bit_shifter u_4_bit_shifter_15 (
    .shift(1'b1), .carry(n4_bit_shifter_19_carry_2), .carry_2(n4_bit_shifter_15_carry_2),
    .out_8(n4_bit_shifter_15_out_8), .out_9(n4_bit_shifter_15_out_9), .out_10(n4_bit_shifter_15_out_10),
    .out_11(n4_bit_shifter_15_out_11), .in_3(not_1_out), .in_4(not_1_out), .in_5(not_1_out), .in_6(not_1_out));
  _4_bit_shifter u_4_bit_shifter_16 (
    .shift(1'b1), .carry(n4_bit_shifter_20_carry_2), .carry_2(n4_bit_shifter_16_carry_2),
    .out_8(n4_bit_shifter_16_out_8), .out_9(n4_bit_shifter_16_out_9), .out_10(n4_bit_shifter_16_out_10),
    .out_11(n4_bit_shifter_16_out_11), .in_3(conditional_adder_9_out_5), .in_4(conditional_adder_9_out_6),
    .in_5(conditional_adder_9_out_7), .in_6(conditional_adder_9_out_8));
  conditional_adder conditional_adder_15 (
    .out_5(conditional_adder_15_out_5), .out_6(conditional_adder_15_out_6),
    .out_7(conditional_adder_15_out_7), .out_8(conditional_adder_15_out_8), .in_1(n4_bit_shifter_23_out_8),
    .in_2(n4_bit_shifter_23_out_9), .in_3(n4_bit_shifter_23_out_10), .in_4(n4_bit_shifter_23_out_11));
  conditional_adder conditional_adder_16 (
    .out_5(conditional_adder_16_out_5), .out_6(conditional_adder_16_out_6),
    .out_7(conditional_adder_16_out_7), .out_8(conditional_adder_16_out_8), .in_1(n4_bit_shifter_24_out_8),
    .in_2(n4_bit_shifter_24_out_9), .in_3(n4_bit_shifter_24_out_10), .in_4(n4_bit_shifter_24_out_11));
  conditional_adder conditional_adder_17 (
    .out_5(conditional_adder_17_out_5), .out_6(conditional_adder_17_out_6),
    .out_7(conditional_adder_17_out_7), .out_8(conditional_adder_17_out_8), .in_1(n4_bit_shifter_17_out_8),
    .in_2(n4_bit_shifter_17_out_9), .in_3(n4_bit_shifter_17_out_10), .in_4(n4_bit_shifter_17_out_11));
  _4_bit_shifter u_4_bit_shifter_17 (
    .shift(1'b1), .carry(main_6_carry_2), .carry_2(n4_bit_shifter_17_carry_2),
    .out_8(n4_bit_shifter_17_out_8), .out_9(n4_bit_shifter_17_out_9), .out_10(n4_bit_shifter_17_out_10),
    .out_11(n4_bit_shifter_17_out_11), .in_3(conditional_adder_18_out_5), .in_4(conditional_adder_18_out_6),
    .in_5(conditional_adder_18_out_7), .in_6(conditional_adder_18_out_8));
  conditional_adder conditional_adder_18 (
    .out_5(conditional_adder_18_out_5), .out_6(conditional_adder_18_out_6),
    .out_7(conditional_adder_18_out_7), .out_8(conditional_adder_18_out_8), .in_1(n4_bit_shifter_18_out_8),
    .in_2(n4_bit_shifter_18_out_9), .in_3(n4_bit_shifter_18_out_10), .in_4(n4_bit_shifter_18_out_11));
  _4_bit_shifter u_4_bit_shifter_18 (
    .shift(1'b1), .carry(main_7_carry_2), .carry_2(n4_bit_shifter_18_carry_2),
    .out_8(n4_bit_shifter_18_out_8), .out_9(n4_bit_shifter_18_out_9), .out_10(n4_bit_shifter_18_out_10),
    .out_11(n4_bit_shifter_18_out_11), .in_3(conditional_adder_19_out_5), .in_4(conditional_adder_19_out_6),
    .in_5(conditional_adder_19_out_7), .in_6(conditional_adder_19_out_8));
  conditional_adder conditional_adder_19 (
    .out_5(conditional_adder_19_out_5), .out_6(conditional_adder_19_out_6),
    .out_7(conditional_adder_19_out_7), .out_8(conditional_adder_19_out_8), .in_1(n4_bit_shifter_19_out_8),
    .in_2(n4_bit_shifter_19_out_9), .in_3(n4_bit_shifter_19_out_10), .in_4(n4_bit_shifter_19_out_11));
  _4_bit_shifter u_4_bit_shifter_19 (
    .shift(not_1_out), .carry(not_1_out), .carry_2(n4_bit_shifter_19_carry_2),
    .out_8(n4_bit_shifter_19_out_8), .out_9(n4_bit_shifter_19_out_9), .out_10(n4_bit_shifter_19_out_10),
    .out_11(n4_bit_shifter_19_out_11), .in_3(not_1_out), .in_4(not_1_out), .in_5(not_1_out),
    .in_6(main_8_carry_2));
  binary_to_0_9_7_segment_signals binary_to_0_9_7_segment_signals_3 (
    .T0(T0_3), .T1(T1_3), .T2(T2_3), .T3(T3_3), .B0(B0_3), .B1(B1_3), .B2(B2_3), .period_2(period_4),
    .in_1(period_1), .in_2(n4_bit_shifter_20_out_9), .in_3(n4_bit_shifter_20_out_10),
    .in_4(n4_bit_shifter_20_out_11), .period(period_2));
  _4_bit_shifter u_4_bit_shifter_20 (
    .shift(1'b1), .carry(main_1_carry_2), .carry_2(n4_bit_shifter_20_carry_2), .out_8(period_1),
    .out_9(n4_bit_shifter_20_out_9), .out_10(n4_bit_shifter_20_out_10), .out_11(n4_bit_shifter_20_out_11),
    .in_3(conditional_adder_20_out_5), .in_4(conditional_adder_20_out_6), .in_5(conditional_adder_20_out_7),
    .in_6(conditional_adder_20_out_8));
  conditional_adder conditional_adder_20 (
    .out_5(conditional_adder_20_out_5), .out_6(conditional_adder_20_out_6),
    .out_7(conditional_adder_20_out_7), .out_8(conditional_adder_20_out_8), .in_1(n4_bit_shifter_21_out_8),
    .in_2(n4_bit_shifter_21_out_9), .in_3(n4_bit_shifter_21_out_10), .in_4(n4_bit_shifter_21_out_11));
  _4_bit_shifter u_4_bit_shifter_21 (
    .shift(1'b1), .carry(main_2_carry_2), .carry_2(n4_bit_shifter_21_carry_2),
    .out_8(n4_bit_shifter_21_out_8), .out_9(n4_bit_shifter_21_out_9), .out_10(n4_bit_shifter_21_out_10),
    .out_11(n4_bit_shifter_21_out_11), .in_3(conditional_adder_21_out_5), .in_4(conditional_adder_21_out_6),
    .in_5(conditional_adder_21_out_7), .in_6(conditional_adder_21_out_8));
  conditional_adder conditional_adder_21 (
    .out_5(conditional_adder_21_out_5), .out_6(conditional_adder_21_out_6),
    .out_7(conditional_adder_21_out_7), .out_8(conditional_adder_21_out_8), .in_1(n4_bit_shifter_22_out_8),
    .in_2(n4_bit_shifter_22_out_9), .in_3(n4_bit_shifter_22_out_10), .in_4(n4_bit_shifter_22_out_11));
  _4_bit_shifter u_4_bit_shifter_22 (
    .shift(1'b1), .carry(main_3_carry_2), .carry_2(n4_bit_shifter_22_carry_2),
    .out_8(n4_bit_shifter_22_out_8), .out_9(n4_bit_shifter_22_out_9), .out_10(n4_bit_shifter_22_out_10),
    .out_11(n4_bit_shifter_22_out_11), .in_3(conditional_adder_15_out_5), .in_4(conditional_adder_15_out_6),
    .in_5(conditional_adder_15_out_7), .in_6(conditional_adder_15_out_8));
  _4_bit_shifter u_4_bit_shifter_23 (
    .shift(1'b1), .carry(main_4_carry_2), .carry_2(n4_bit_shifter_23_carry_2),
    .out_8(n4_bit_shifter_23_out_8), .out_9(n4_bit_shifter_23_out_9), .out_10(n4_bit_shifter_23_out_10),
    .out_11(n4_bit_shifter_23_out_11), .in_3(conditional_adder_16_out_5), .in_4(conditional_adder_16_out_6),
    .in_5(conditional_adder_16_out_7), .in_6(conditional_adder_16_out_8));
  _4_bit_shifter u_4_bit_shifter_24 (
    .shift(1'b1), .carry(main_5_carry_2), .carry_2(n4_bit_shifter_24_carry_2),
    .out_8(n4_bit_shifter_24_out_8), .out_9(n4_bit_shifter_24_out_9), .out_10(n4_bit_shifter_24_out_10),
    .out_11(n4_bit_shifter_24_out_11), .in_3(conditional_adder_17_out_5), .in_4(conditional_adder_17_out_6),
    .in_5(conditional_adder_17_out_7), .in_6(conditional_adder_17_out_8));
  _8_bit_left_shifter_main main_1 (
    .shift(not_1_out), .carry(1'b1), .carry_2(main_1_carry_2), .in_3(main_2_out_12), .in_4(main_2_out_13),
    .in_5(main_2_out_14), .in_6(main_2_out_15), .in_7(main_2_out_16), .in_8(main_2_out_17),
    .in_9(main_2_out_18), .in_10(main_2_out_19));  // open: out_12, out_13, out_14, out_15, out_16, out_17, out_18, out_19
  _8_bit_left_shifter_main main_2 (
    .shift(1'b1), .carry(not_1_out), .carry_2(main_2_carry_2), .out_12(main_2_out_12),
    .out_13(main_2_out_13), .out_14(main_2_out_14), .out_15(main_2_out_15), .out_16(main_2_out_16),
    .out_17(main_2_out_17), .out_18(main_2_out_18), .out_19(main_2_out_19), .in_3(main_3_out_12),
    .in_4(main_3_out_13), .in_5(main_3_out_14), .in_6(main_3_out_15), .in_7(main_3_out_16),
    .in_8(main_3_out_17), .in_9(main_3_out_18), .in_10(main_3_out_19));
  _8_bit_left_shifter_main main_3 (
    .shift(1'b1), .carry(not_1_out), .carry_2(main_3_carry_2), .out_12(main_3_out_12),
    .out_13(main_3_out_13), .out_14(main_3_out_14), .out_15(main_3_out_15), .out_16(main_3_out_16),
    .out_17(main_3_out_17), .out_18(main_3_out_18), .out_19(main_3_out_19), .in_3(main_4_out_12),
    .in_4(main_4_out_13), .in_5(main_4_out_14), .in_6(main_4_out_15), .in_7(main_4_out_16),
    .in_8(main_4_out_17), .in_9(main_4_out_18), .in_10(main_4_out_19));
  _8_bit_left_shifter_main main_4 (
    .shift(1'b1), .carry(not_1_out), .carry_2(main_4_carry_2), .out_12(main_4_out_12),
    .out_13(main_4_out_13), .out_14(main_4_out_14), .out_15(main_4_out_15), .out_16(main_4_out_16),
    .out_17(main_4_out_17), .out_18(main_4_out_18), .out_19(main_4_out_19), .in_3(main_5_out_12),
    .in_4(main_5_out_13), .in_5(main_5_out_14), .in_6(main_5_out_15), .in_7(main_5_out_16),
    .in_8(main_5_out_17), .in_9(main_5_out_18), .in_10(main_5_out_19));
  _8_bit_left_shifter_main main_5 (
    .shift(1'b1), .carry(not_1_out), .carry_2(main_5_carry_2), .out_12(main_5_out_12),
    .out_13(main_5_out_13), .out_14(main_5_out_14), .out_15(main_5_out_15), .out_16(main_5_out_16),
    .out_17(main_5_out_17), .out_18(main_5_out_18), .out_19(main_5_out_19), .in_3(main_6_out_12),
    .in_4(main_6_out_13), .in_5(main_6_out_14), .in_6(main_6_out_15), .in_7(main_6_out_16),
    .in_8(main_6_out_17), .in_9(main_6_out_18), .in_10(main_6_out_19));
  _8_bit_left_shifter_main main_6 (
    .shift(1'b1), .carry(not_1_out), .carry_2(main_6_carry_2), .out_12(main_6_out_12),
    .out_13(main_6_out_13), .out_14(main_6_out_14), .out_15(main_6_out_15), .out_16(main_6_out_16),
    .out_17(main_6_out_17), .out_18(main_6_out_18), .out_19(main_6_out_19), .in_3(main_7_out_12),
    .in_4(main_7_out_13), .in_5(main_7_out_14), .in_6(main_7_out_15), .in_7(main_7_out_16),
    .in_8(main_7_out_17), .in_9(main_7_out_18), .in_10(main_7_out_19));
  _8_bit_left_shifter_main main_7 (
    .shift(1'b1), .carry(not_1_out), .carry_2(main_7_carry_2), .out_12(main_7_out_12),
    .out_13(main_7_out_13), .out_14(main_7_out_14), .out_15(main_7_out_15), .out_16(main_7_out_16),
    .out_17(main_7_out_17), .out_18(main_7_out_18), .out_19(main_7_out_19), .in_3(main_8_out_12),
    .in_4(main_8_out_13), .in_5(main_8_out_14), .in_6(main_8_out_15), .in_7(main_8_out_16),
    .in_8(main_8_out_17), .in_9(main_8_out_18), .in_10(main_8_out_19));
  _8_bit_left_shifter_main main_8 (
    .shift(1'b1), .carry(not_1_out), .carry_2(main_8_carry_2), .out_12(main_8_out_12),
    .out_13(main_8_out_13), .out_14(main_8_out_14), .out_15(main_8_out_15), .out_16(main_8_out_16),
    .out_17(main_8_out_17), .out_18(main_8_out_18), .out_19(main_8_out_19), .in_3(in_4), .in_4(in_5),
    .in_5(in_6), .in_6(in_7), .in_7(in_8), .in_8(in_9), .in_9(in_10), .in_10(in_11));
endmodule

module binary_to_0_9_decimal_signal (
  input  in_1,
  input  in_2,
  input  in_3,
  input  in_4,
  output _9,
  output _8,
  output _7,
  output _6,
  output _5,
  output _4,
  output _3,
  output _2,
  output _1,
  output _0
);

  wire not_1_out, not_2_out, not_3_out, not_4_out;

  not not_1 (not_1_out, in_1);
  not not_2 (not_2_out, in_2);
  not not_3 (not_3_out, in_4);
  not not_4 (not_4_out, in_3);
  and u__9 (_9, in_1, not_2_out, not_4_out, in_4);
  and u__8 (_8, in_1, not_2_out, not_4_out, not_3_out);
  and u__7 (_7, not_1_out, in_2, in_3, in_4);
  and u__6 (_6, not_1_out, in_2, in_3, not_3_out);
  and u__5 (_5, not_1_out, in_2, not_4_out, in_4);
  and u__4 (_4, not_1_out, in_2, not_4_out, not_3_out);
  and u__3 (_3, not_1_out, not_2_out, in_3, in_4);
  and u__2 (_2, not_1_out, not_2_out, in_3, not_3_out);
  and u__1 (_1, not_1_out, not_2_out, not_4_out, in_4);
  and u__0 (_0, not_1_out, not_2_out, not_4_out, not_3_out);
endmodule

module binary_to_0_9_7_segment_signals (
  input  in_1,
  input  in_2,
  input  in_3,
  input  in_4,
  input  period,
  output T0,
  output T1,
  output T2,
  output T3,
  output B0,
  output B1,
  output B2,
  output period_2
);

  wire binary_to_0_9_decimal_signal_1__0, binary_to_0_9_decimal_signal_1__1,
       binary_to_0_9_decimal_signal_1__2, binary_to_0_9_decimal_signal_1__3,
       binary_to_0_9_decimal_signal_1__4, binary_to_0_9_decimal_signal_1__5,
       binary_to_0_9_decimal_signal_1__6, binary_to_0_9_decimal_signal_1__7,
       binary_to_0_9_decimal_signal_1__8, binary_to_0_9_decimal_signal_1__9;

  binary_to_0_9_decimal_signal binary_to_0_9_decimal_signal_1 (
    ._9(binary_to_0_9_decimal_signal_1__9), ._8(binary_to_0_9_decimal_signal_1__8),
    ._7(binary_to_0_9_decimal_signal_1__7), ._6(binary_to_0_9_decimal_signal_1__6),
    ._5(binary_to_0_9_decimal_signal_1__5), ._4(binary_to_0_9_decimal_signal_1__4),
    ._3(binary_to_0_9_decimal_signal_1__3), ._2(binary_to_0_9_decimal_signal_1__2),
    ._1(binary_to_0_9_decimal_signal_1__1), .in_1(in_1), .in_2(in_2), .in_3(in_3), .in_4(in_4),
    ._0(binary_to_0_9_decimal_signal_1__0));
  or u_T0 (T0, binary_to_0_9_decimal_signal_1__2, binary_to_0_9_decimal_signal_1__3, binary_to_0_9_decimal_signal_1__4, binary_to_0_9_decimal_signal_1__5, binary_to_0_9_decimal_signal_1__6, binary_to_0_9_decimal_signal_1__8, binary_to_0_9_decimal_signal_1__9);
  or u_T1 (T1, binary_to_0_9_decimal_signal_1__0, binary_to_0_9_decimal_signal_1__4, binary_to_0_9_decimal_signal_1__5, binary_to_0_9_decimal_signal_1__6, binary_to_0_9_decimal_signal_1__8, binary_to_0_9_decimal_signal_1__9);
  or u_T2 (T2, binary_to_0_9_decimal_signal_1__0, binary_to_0_9_decimal_signal_1__2, binary_to_0_9_decimal_signal_1__3, binary_to_0_9_decimal_signal_1__5, binary_to_0_9_decimal_signal_1__6, binary_to_0_9_decimal_signal_1__7, binary_to_0_9_decimal_signal_1__8, binary_to_0_9_decimal_signal_1__9);
  or u_T3 (T3, binary_to_0_9_decimal_signal_1__0, binary_to_0_9_decimal_signal_1__1, binary_to_0_9_decimal_signal_1__2, binary_to_0_9_decimal_signal_1__3, binary_to_0_9_decimal_signal_1__4, binary_to_0_9_decimal_signal_1__7, binary_to_0_9_decimal_signal_1__8, binary_to_0_9_decimal_signal_1__9);
  or u_B0 (B0, binary_to_0_9_decimal_signal_1__0, binary_to_0_9_decimal_signal_1__2, binary_to_0_9_decimal_signal_1__6, binary_to_0_9_decimal_signal_1__8);
  or u_B1 (B1, binary_to_0_9_decimal_signal_1__0, binary_to_0_9_decimal_signal_1__2, binary_to_0_9_decimal_signal_1__3, binary_to_0_9_decimal_signal_1__5, binary_to_0_9_decimal_signal_1__6, binary_to_0_9_decimal_signal_1__8, binary_to_0_9_decimal_signal_1__9);
  or u_B2 (B2, binary_to_0_9_decimal_signal_1__0, binary_to_0_9_decimal_signal_1__1, binary_to_0_9_decimal_signal_1__3, binary_to_0_9_decimal_signal_1__4, binary_to_0_9_decimal_signal_1__5, binary_to_0_9_decimal_signal_1__6, binary_to_0_9_decimal_signal_1__7, binary_to_0_9_decimal_signal_1__8, binary_to_0_9_decimal_signal_1__9);

  assign period_2 = period;
endmodule

module conditional_adder (
  input  in_1,
  input  in_2,
  input  in_3,
  input  in_4,
  output out_5,
  output out_6,
  output out_7,
  output out_8
);

  wire and_1_out, and_2_out, and_3_out, main_1_out_19, main_2_out_23, main_2_out_24, main_2_out_25,
       main_2_out_26, not_1_out, not_2_out, not_3_out, or_1_out;

  _2_bit_multiplexer u_2_bit_multiplexer_1 (.S___A___0__B___1(or_1_out), .A(main_2_out_23), .B(in_1), .R(out_5));
  _8_bit_full_adder_main main_1 (
    .in_1(1'b1), .in_2(not_1_out), .in_3(1'b1), .in_4(not_1_out), .in_5(1'b1), .in_6(not_1_out), .in_7(1'b1),
    .in_8(not_1_out), .in_9(1'b1), .in_10(in_1), .in_11(not_1_out), .in_12(in_2), .in_13(1'b1), .in_14(in_3),
    .in_15(not_1_out), .in_16(in_4), .carry(not_1_out), .out_19(main_1_out_19));  // open: out_20, out_21, out_22, out_23, out_24, out_25, out_26, carry_2
  not not_1 (not_1_out, 1'b1);
  _2_bit_multiplexer u_2_bit_multiplexer_2 (.S___A___0__B___1(or_1_out), .A(main_2_out_24), .B(in_2), .R(out_6));
  _2_bit_multiplexer u_2_bit_multiplexer_3 (.S___A___0__B___1(or_1_out), .A(main_2_out_25), .B(in_3), .R(out_7));
  _8_bit_full_adder_main main_2 (
    .in_1(not_1_out), .in_2(not_1_out), .in_3(not_1_out), .in_4(not_1_out), .in_5(not_1_out),
    .in_6(not_1_out), .in_7(not_1_out), .in_8(not_1_out), .in_9(in_1), .in_10(not_1_out), .in_11(in_2),
    .in_12(not_1_out), .in_13(in_3), .in_14(1'b1), .in_15(in_4), .in_16(1'b1), .carry(not_1_out),
    .out_23(main_2_out_23), .out_24(main_2_out_24), .out_25(main_2_out_25), .out_26(main_2_out_26));  // open: out_19, out_20, out_21, out_22, carry_2
  _2_bit_multiplexer u_2_bit_multiplexer_4 (.S___A___0__B___1(or_1_out), .A(main_2_out_26), .B(in_4), .R(out_8));
  or or_1 (or_1_out, and_3_out, and_1_out);
  and and_1 (and_1_out, not_2_out, not_3_out);
  not not_2 (not_2_out, main_1_out_19);
  not not_3 (not_3_out, and_2_out);
  and and_2 (and_2_out, ~in_1, ~in_2, ~in_3, ~in_4);  // AND_Gate
  and and_3 (and_3_out, ~in_1, in_2, ~in_3, in_4);  // AND_Gate
endmodule

module _2_bit_multiplexer (
  input  S___A___0__B___1,
  input  A,
  input  B,
  output R
);

  wire and_1_out, and_2_out, not_1_out;

  and and_1 (and_1_out, A, S___A___0__B___1);
  or or_1 (R, and_1_out, and_2_out);
  and and_2 (and_2_out, B, not_1_out);
  not not_1 (not_1_out, S___A___0__B___1);
endmodule
