// Logisim project 8-bit left shifter.circ as structural Verilog: 3 circuits, main circuit main
module main (
  input  shift,
  input  carry,
  input  in_3,
  input  in_4,
  input  in_5,
  input  in_6,
  input  in_7,
  input  in_8,
  input  in_9,
  input  in_10,
  output carry_2,
  output out_12,
  output out_13,
  output out_14,
  output out_15,
  output out_16,
  output out_17,
  output out_18,
  output out_19
);

  wire n4_bit_shifter_2_carry_2;

  _4_bit_shifter u_4_bit_shifter_1 (
    .shift(shift), .carry(n4_bit_shifter_2_carry_2), .carry_2(carry_2), .out_8(out_12), .out_9(out_13),
    .out_10(out_14), .out_11(out_15), .in_3(in_3), .in_4(in_4), .in_5(in_5), .in_6(in_6));
  _4_bit_shifter u_4_bit_shifter_2 (
    .shift(shift), .carry(carry), .carry_2(n4_bit_shifter_2_carry_2), .out_8(out_16), .out_9(out_17),
    .out_10(out_18), .out_11(out_19), .in_3(in_7), .in_4(in_8), .in_5(in_9), .in_6(in_10));
endmodule

module _1_bit_shifter (
  input  shift,
  input  in_2,
  input  carry,
  output carry_2,
  output out_5
);

  wire and_1_out, and_2_out, not_1_out;

  or or_1 (out_5, and_1_out, and_2_out);
  and and_1 (and_1_out, in_2, not_1_out);
  not not_1 (not_1_out, shift);
  and and_2 (and_2_out, carry, shift);

  assign carry_2 = in_2;
endmodule

module _4_bit_shifter (
  input  shift,
  input  carry,
  input  in_3,
  input  in_4,
  input  in_5,
  input  in_6,
  output carry_2,
  output out_8,
  output out_9,
  output out_10,
  output out_11
);

  wire n1_bit_shifter_2_carry_2, n1_bit_shifter_3_carry_2, n1_bit_shifter_4_carry_2;

  _1_bit_shifter u_1_bit_shifter_1 (
    .shift(shift), .carry(n1_bit_shifter_2_carry_2), .in_2(in_3), .out_5(out_8), .carry_2(carry_2));
  _1_bit_shifter u_1_bit_shifter_2 (
    .shift(shift), .carry(n1_bit_shifter_3_carry_2), .in_2(in_4), .out_5(out_9),
    .carry_2(n1_bit_shifter_2_carry_2));
  _1_bit_shifter u_1_bit_shifter_3 (
    .shift(shift), .carry(n1_bit_shifter_4_carry_2), .in_2(in_5), .out_5(out_10),
    .carry_2(n1_bit_shifter_3_carry_2));
  _1_bit_shifter u_1_bit_shifter_4 (
    .shift(shift), .carry(carry), .in_2(in_6), .out_5(out_11), .carry_2(n1_bit_shifter_4_carry_2));
endmodule
